// Logisim project mmarc-one-logic-array.circ as structural Verilog: 1 circuit, main circuit main
module main (
);

  wire and_1_out, and_2_out, and_3_out, and_4_out, and_5_out, and_6_out, and_7_out, and_8_out, and_9_out,
       bitselector_1_out, bitselector_2_out, bitselector_3_out, button_1_out, clock_1_out, clock_2_out,
       comparator_1_eq, not_1_out, not_2_out, not_3_out, not_4_out, not_5_out, or_1_out, or_2_out, or_3_out;
  wire [2:0] bit_extender_1_out;
  wire [3:0] bitselector_4_out, bitselector_5_out, bitselector_6_out, bitselector_7_out;
  wire [12:0] adder_1_out, adder_2_out, bit_extender_2_out, bit_extender_5_out, bit_extender_7_out,
       multiplexer_1_out, multiplexer_4_out, multiplexer_5_out, multiplexer_6_out, multiplexer_9_out, PC_q,
       ram_1_data, ReadOutput_q;
  wire [15:0] Accumulator_q, adder_3_out, bit_extender_3_out, bit_extender_4_out, bit_extender_6_out,
       multiplexer_2_out, multiplexer_3_out, multiplexer_7_out, multiplexer_8_out, rom_1_data, shifter_1_out,
       subtractor_1_out;

  Shifter #(.width(16), .shift("lr")) shifter_1 (.in(rom_1_data), .\dist (4'b1101), .out(shifter_1_out));
  Bit_Extender #(.in_width(16), .out_width(3)) bit_extender_1 (.in(shifter_1_out), .out(bit_extender_1_out));
  BitSelector #(.width(3)) bitselector_1 (.in(bit_extender_1_out), .out(bitselector_1_out), .sel(2'b10));
  BitSelector #(.width(3)) bitselector_2 (.in(bit_extender_1_out), .out(bitselector_2_out), .sel(2'b01));
  BitSelector #(.width(3)) bitselector_3 (.in(bit_extender_1_out), .out(bitselector_3_out), .sel(2'b00));
  Clock #(.highDuration(2), .lowDuration(2)) clock_1 (.out(clock_1_out));
  LED led_1 (.in(bitselector_1_out));
  LED led_2 (.in(bitselector_2_out));
  LED led_3 (.in(bitselector_3_out));
  Register #(.width(13)) PC (.D(multiplexer_1_out), .en(1'b1), .Q(PC_q), .clk(clock_1_out), .clr(button_1_out));
  not not_1 (not_1_out, bitselector_3_out);
  Button button_1 (.out(button_1_out));
  Adder #(.width(13)) adder_1 (.a(13'h1), .b(PC_q), .out(adder_1_out));  // open: cin, cout
  not not_2 (not_2_out, bitselector_2_out);
  Adder #(.width(13)) adder_2 (.a(adder_1_out), .b(bit_extender_2_out), .out(adder_2_out));  // open: cin, cout
  not not_3 (not_3_out, bitselector_1_out);
  Multiplexer #(.width(13), .enable("false")) multiplexer_1 (
    .in0(adder_1_out), .in1(adder_2_out), .out(multiplexer_1_out), .sel(and_9_out));
  ROM #(.addrWidth(13), .dataWidth(16)) rom_1 (.addr(PC_q), .data(rom_1_data), .sel(1'b1));
  and and_1 (and_1_out, not_3_out, not_2_out, not_1_out);
  and and_2 (and_2_out, bitselector_1_out, bitselector_2_out);
  and and_3 (and_3_out, not_3_out, not_2_out, bitselector_3_out);
  and and_4 (and_4_out, not_3_out, bitselector_2_out, not_1_out);
  and and_5 (and_5_out, bitselector_2_out, bitselector_3_out);
  and and_6 (and_6_out, bitselector_3_out, not_2_out);
  and and_7 (and_7_out, not_1_out, bitselector_2_out);
  and and_8 (and_8_out, bitselector_1_out, bitselector_2_out);
  and and_9 (and_9_out, comparator_1_eq, and_1_out);
  LED led_4 (.in(and_1_out));
  LED led_5 (.in(and_2_out));
  LED led_6 (.in(bitselector_3_out));
  or or_1 (or_1_out, and_3_out, and_4_out);
  LED led_7 (.in(or_1_out));
  LED led_8 (.in(or_2_out));
  or or_2 (or_2_out, and_5_out, bitselector_1_out);
  LED led_9 (.in(not_3_out));
  or or_3 (or_3_out, and_6_out, not_3_out);
  LED led_10 (.in(not_2_out));
  LED led_11 (.in(and_7_out));
  LED led_12 (.in(and_8_out));
  LED led_13 (.in(not_2_out));
  Bit_Extender #(.in_width(16), .out_width(13)) bit_extender_2 (.in(rom_1_data), .out(bit_extender_2_out));
  LED led_14 (.in(or_3_out));
  assign bit_extender_3_out = {{3{bit_extender_2_out[12]}}, bit_extender_2_out};  // Bit_Extender bit_extender_3
  Register #(.width(16)) Accumulator (
    .D(multiplexer_7_out), .en(or_2_out), .Q(Accumulator_q), .clk(clock_1_out));  // open: clr
  Multiplexer #(.width(16), .enable("false")) multiplexer_2 (
    .in0(bit_extender_3_out), .in1(bit_extender_4_out), .out(multiplexer_2_out), .sel(or_3_out));
  assign bit_extender_4_out = {{3{ram_1_data[12]}}, ram_1_data};  // Bit_Extender bit_extender_4
  Multiplexer #(.width(16), .enable("false")) multiplexer_3 (
    .in0(multiplexer_8_out), .in1(bit_extender_6_out), .out(multiplexer_3_out), .sel(and_2_out));
  Adder #(.width(16)) adder_3 (.a(Accumulator_q), .b(multiplexer_2_out), .out(adder_3_out));  // open: cin, cout
  Subtractor #(.width(16)) subtractor_1 (
    .a(Accumulator_q), .b(multiplexer_2_out), .out(subtractor_1_out));  // open: bin, bout
  Multiplexer #(.width(13), .enable("false")) multiplexer_4 (
    .in0(bit_extender_2_out), .in1(bit_extender_5_out), .out(multiplexer_4_out), .sel(and_8_out));
  Multiplexer #(.width(13), .enable("false")) multiplexer_5 (
    .in0(multiplexer_4_out), .in1(multiplexer_6_out), .out(multiplexer_5_out), .sel(not_4_out));
  not not_4 (not_4_out, clock_2_out);
  Multiplexer #(.width(13), .enable("false")) multiplexer_6 (
    .in0(bit_extender_2_out), .in1(bit_extender_7_out), .out(multiplexer_6_out), .sel(not_2_out));
  Multiplexer #(.width(16), .enable("false")) multiplexer_7 (
    .in0(multiplexer_3_out), .in1(bit_extender_3_out), .out(multiplexer_7_out), .sel(and_7_out));
  Multiplexer #(.width(16), .enable("false")) multiplexer_8 (
    .in0(adder_3_out), .in1(subtractor_1_out), .out(multiplexer_8_out), .sel(not_3_out));
  Bit_Extender #(.in_width(16), .out_width(13), .\type ("sign")) bit_extender_5 (
    .in(multiplexer_8_out), .out(bit_extender_5_out));
  Comparator #(.width(16)) comparator_1 (.a(Accumulator_q), .b({16{1'b0}}), .eq(comparator_1_eq));  // open: gt, lt
  RAM #(.addrWidth(13), .dataWidth(13), .bus("separate")) ram_1 (
    .addr(multiplexer_5_out), .din(multiplexer_9_out), .data(ram_1_data), .str(or_1_out), .sel(1'b1),
    .clk(clock_2_out), .ld(bitselector_3_out));  // open: clr
  Multiplexer #(.width(13), .enable("false")) multiplexer_9 (
    .in0(bit_extender_7_out), .in1(ReadOutput_q), .out(multiplexer_9_out), .sel(not_2_out));
  assign bit_extender_6_out = {{3{ram_1_data[12]}}, ram_1_data};  // Bit_Extender bit_extender_6
  Register #(.width(13)) ReadOutput (
    .D(ram_1_data), .en(bitselector_3_out), .Q(ReadOutput_q), .clk(not_5_out));  // open: clr
  Hex_Digit_Display hex_digit_display_1 (.value(bitselector_4_out));  // open: dp
  BitSelector #(.width(16), .group(4)) bitselector_4 (.in(Accumulator_q), .out(bitselector_4_out), .sel(2'b11));
  Bit_Extender #(.in_width(16), .out_width(13), .\type ("sign")) bit_extender_7 (
    .in(Accumulator_q), .out(bit_extender_7_out));
  not not_5 (not_5_out, clock_2_out);
  Clock clock_2 (.out(clock_2_out));
  Hex_Digit_Display hex_digit_display_2 (.value(bitselector_5_out));  // open: dp
  BitSelector #(.width(16), .group(4)) bitselector_5 (.in(Accumulator_q), .out(bitselector_5_out), .sel(2'b10));
  Hex_Digit_Display hex_digit_display_3 (.value(bitselector_6_out));  // open: dp
  BitSelector #(.width(16), .group(4)) bitselector_6 (.in(Accumulator_q), .out(bitselector_6_out), .sel(2'b01));
  Hex_Digit_Display hex_digit_display_4 (.value(bitselector_7_out));  // open: dp
  BitSelector #(.width(16), .group(4)) bitselector_7 (.in(Accumulator_q), .out(bitselector_7_out), .sel(2'b00));

  // Notes on the sheet:
  //   b2
  //   b1
  //   b0
  //   Instruction Memory
  //   contents of rom_1 (hex, n*v repeats v):
  //   c000 e000 1e c000 e100 e000 4400 c000 e200 e000 a400 4400 c000 e300 2400 c000 e100 8001 4100 c000
  //   e200 8001 4200 c000 e300 8001 4300 c000 e000 9fff 4000 c000 1fdf 1fff
  //   Branch
  //   mem sel
  //   write en
  //   accum write
  //   alu op
  //   in sel
  //   imm sel
  //   offset en
  //   read en
  //   alu src
  //   write sel
  //   Write en
  //   alu sel
  //   mem sel
  //   offset en
  //   write sel
  //   imm sel
  //   0 - read, 1 -write
  //   alu op
  //   zero
  //   in sel
endmodule
